# Fritzing sketch Burgler_Alarm (saved by Fritzing 0.9.2b)

parts:
  Grove1 = Grove Buzz
  Grove2 = Grove Infrared Receiver
  Grove3 = Grove Infrared Emitter
  Grove4 = Grove Light Sensor
  Part1 = Intel Galileo Gen2
  Part2 = Base Shield V2
  Grove5 = Grove Button

nets:
  N1: Grove1.GND, Part2.pin_120, Part2.pin_143
  N2: Grove1.VCC, Part2.pin_121
  N3: Grove1.SIG, Part2.pin_123
  N4: Grove2.GND, Part2.pin_155
  N5: Grove2.VCC, Part2.pin_154
  N6: Grove2.RX, Part2.pin_153
  N7: Grove3.GND, Part2.pin_116
  N8: Grove3.VCC, Part2.pin_117
  N9: Grove3.TX, Part2.pin_119
  N10: Grove4.GND, Part2.pin_96
  N11: Grove4.VCC, Part2.pin_97
  N12: Grove4.SIG, Part2.pin_99
  N13: Part1.A0, Part2.A0
  N14: Part1.A1, Part2.A1
  N15: Part1.A2, Part2.A2
  N16: Part1.A3, Part2.A3
  N17: Part1.A4/SDA, Part2.A4
  N18: Part1.A5/SCL, Part2.A5
  N19: Part1.D8, Part2.D8
  N20: Part1.D9_PWM, Part2.D9
  N21: Part1.D10_PWM/SS, Part2.D10
  N22: Part1.D11_PWM/MOSI, Part2.D11
  N23: Part1.D12/MISO, Part2.D12
  N24: Part1.D13/SCK, Part2.D13
  GND: Part1.GND, Part2.GND
  N25: Part1.AREF, Part2.AREF
  N26: Part1.D0/RX, Part2.D0/RX
  N27: Part1.D1/TX, Part2.D1/TX
  N28: Part1.D2, Part2.D2
  N29: Part1.D3_PWM, Part2.D3
  N30: Part1.D4, Part2.D4
  N31: Part1.D5_PWM, Part2.D5
  N32: Part1.D6_PWM, Part2.D6_PWM
  N33: Part1.D7, Part2.D7
  N34: Part1.ioref, Part2.ioref
  N35: Part1.RESET, Part2.RESET
  3V3: Part1.3V3, Part2.3V3
  5V: Part1.5V, Part2.5V
  VIN: Part1.VIN, Part2.VIN
  N36: Part1.N/C, Part2.N/C
  N37: Part2.pin_112, Grove5.GND
  N38: Part2.pin_113, Grove5.VCC
  N39: Part2.pin_114, Grove5.NC
  N40: Part2.pin_115, Grove5.SIG

// code stored in the sketch: Burgler_Alarm.ino
int led=13;
int light=2;
int acc=3;
int infra_r=A3;
int infra_e=7;
int buzz=8;
int touch=6;
void setup()
{
	pinMode(led, OUTPUT);
	pinMode(light, INPUT);
	pinMode(buzz, OUTPUT);
	pinMode(infra_r, INPUT);
	pinMode(infra_e, OUTPUT);
	pinMode(acc, INPUT);
	Serial.begin(9600);
}
void loop()
{
	if(light>0)
	{
		int val=analogRead(infra_r);
		Serial.println(val);
		if(val>=1005)
		{
			
		if(digitalRead(touch))
		{
			digitalWrite(led, HIGH);
			digitalWrite(buzz, HIGH);
			delay(500);
			digitalWrite(led, LOW);
			digitalWrite(buzz, HIGH);
		}
		}
	}
	else
	{
		digitalWrite(led, LOW);
		digitalWrite(buzz, LOW);
	}
}
